# Fritzing sketch MasterSlaveSolarTracker (saved by Fritzing 0.9.3b)
breadboards: 2

parts:
  R1 = Photocell (LDR) [package=THT]
  R2 = Photocell (LDR) [package=THT]
  R3 = Photocell (LDR) [package=THT]
  R5 = Resistor [tolerance=±5% resistance=22k package="2010 [SMD]"]
  R6 = Resistor [tolerance=±5% resistance=22k package="2010 [SMD]"]
  R8 = Resistor [tolerance=±5% resistance=22k package="2010 [SMD]"]
  R9 = Resistor [tolerance=±5% resistance=10k package="2010 [SMD]"]
  R10 = Resistor [tolerance=±5% resistance=10k package="2010 [SMD]"]
  S1 = Momentary Switch [package=ksa_sealed_tac_switch]
  S2 = Momentary Switch [package=ksa_sealed_tac_switch]
  R4 = Photocell (LDR) [package=THT]
  Part1 = Solar Charge Controller [part_number="HGX Series Solar Charge Controller PWM" package=PWM-Model]
  Part2 = Solar Panel [package="Renogy 50 Watts 12 Volt Monocrystalline Bendable Solar Panel"]
  Part3 = Arduino Nano (Rev3.0)
  R11 = Resistor [tolerance=±5% resistance=22k package="2010 [SMD]"]
  U2 = NodeMCU V1.0
  R12 = Resistor [tolerance=±5% resistance=10k package="2010 [SMD]"]
  R13 = Resistor [tolerance=±5% resistance=100k package="2010 [SMD]"]
  C1 = Capacitor Polarized [package=panasonic_c]
  C2 = Capacitor Polarized [package=panasonic_c]  # not connected
  S3 = Toggle Switch [package=THT]
  S4 = Toggle Switch [package=THT]
  R14 = Resistor [tolerance=±5% resistance=10k package="2010 [SMD]"]
  R15 = Resistor [tolerance=±5% resistance=10k package="2010 [SMD]"]
  M1 = DC Motor
  S5 = H-Bridge with L298N
  F1 = FUSE [package=fuse_5mm]
  D2F1 = D2F-FL Omron Snap Action Limit Switch with Level
  D2F2 = D2F-FL Omron Snap Action Limit Switch with Level
  R16 = Resistor [tolerance=±5% resistance=10k package="2010 [SMD]"]  # not connected
  R17 = Resistor [tolerance=±5% resistance=10k package="2010 [SMD]"]
  R18 = Resistor [tolerance=±5% resistance=220 package="2512 [SMD]"]
  LED1 = smd LED [color="Green (555nm)" package="0805 [SMD]"]
  LED2 = smd LED [color="Red (633nm)" package="0805 [SMD]"]
  LED3 = smd LED [color="Green (555nm)" package="0805 [SMD]"]
  R19 = Resistor [tolerance=±5% resistance=220 package="2512 [SMD]"]
  R20 = Resistor [tolerance=±5% resistance=220 package="2512 [SMD]"]
  2_Channel_Relay1 = 2 Channel Power Relay
  KY-1 = Keyes Relay [package=THT]
  LCD1 = 20x4 LCD display [part_number=2004A]
  Power_plug2 = Power plug
  ACS712_Current_Sensor1 = ACS712 Current Sensor
  LCM1602_IIC1 = LCM1602 IIC [part_number="LCM1602 IIC" chip_label="LCM1602 IIC" package="DIP (Dual Inline) [THT]"]
  D2F3 = D2F-FL Omron Snap Action Limit Switch with Level
  R21 = Resistor [tolerance=±5% resistance=10k package="2010 [SMD]"]
  R22 = Resistor [tolerance=±5% resistance=220 package="2512 [SMD]"]
  R23 = Resistor [tolerance=±5% resistance=220 package="2512 [SMD]"]
  LED4 = smd LED [color="Green (555nm)" package="0805 [SMD]"]  # not connected
  LED5 = smd LED [color="Green (555nm)" package="0805 [SMD]"]  # not connected
  M2 = DC Motor
  Power_plug3 = Power plug
  Power_plug4 = Power plug
  Power_plug5 = Power plug
  R24 = Photocell (LDR) [package=THT]

nets:
  N1: R1.pin_0, R6.Pin_1, Part3.A2
  N2: R2.pin_0, S2.3, R4.pin_0, ACS712_Current_Sensor1.VCC, R24.pin_0
  N3: R2.pin_1, R5.Pin_0, Part3.A3
  N4: R3.pin_0, R8.Pin_1, Part3.A0
  GND: R5.Pin_1, R6.Pin_0, R8.Pin_0, R9.Pin_1, R10.Pin_0, Part3.GND, R11.Pin_1, U2.GND, R14.Pin_0, R15.Pin_1, R17.Pin_0, Power_plug2.GND, ACS712_Current_Sensor1.GND
  N5: R9.Pin_0, S2.1
  N6: R10.Pin_1, S1.3
  N7: R4.pin_1, Part3.A1, R11.Pin_0, R24.pin_1
  N8: Part1.Connector_2, Part2.Connector_2
  N9: Part1.Connector_3, R13.Pin_1
  N10: Part1.Connector_4, R12.Pin_0, C1.-
  N11: Part3.D1/TX, U2.D6
  N12: Part3.D0/RX, U2.D7
  N13: Part3.D4, S4.L2
  N14: Part3.D5, S3.COM
  N15: Part3.D6, D2F2.NO
  N16: Part3.D7, D2F1.NO
  N17: Part3.D8, S5.ENA
  N18: Part3.D9, S5.IN1
  N19: Part3.D10, S5.IN2
  N20: Part3.D11/MOSI, R18.Pin_0
  N21: Part3.D12/MISO, R19.Pin_0
  5V: Part3.5V, U2.Vin, Power_plug2.VCC
  N22: Part3.A5, ACS712_Current_Sensor1.OUT
  N23: Part3.A4, R12.Pin_1, R13.Pin_0, C1.+
  N24: Part3.D13/SCK, R20.Pin_0
  N25: U2.D0, D2F3.COM
  N26: U2.D1, LCM1602_IIC1.SCL
  N27: U2.D2, LCM1602_IIC1.SDA
  N28: U2.D3, R22.Pin_0
  N29: U2.D4, R23.Pin_0
  N30: U2.D5, 2_Channel_Relay1.IN1
  N31: U2.D8, KY-1.power
  N32: S3.L2, R15.Pin_0
  N33: S4.COM, R14.Pin_1
  N34: M1.pin_1, S5.M1-02
  N35: M1.pin_2, S5.M1-01
  N36: S5.12V, F1.1
  N37: LED1.cathode, LED2.cathode, LED3.cathode
  N38: 2_Channel_Relay1.GND, R21.Pin_0
  N39: 2_Channel_Relay1.K1-NC, Power_plug3.GND
  N40: 2_Channel_Relay1.K1-COM, M2.pin_1
  N41: 2_Channel_Relay1.K1-NO, Power_plug4.GND
  N42: 2_Channel_Relay1.K2-NC, KY-1.NO
  N43: 2_Channel_Relay1.K2-COM, M2.pin_2
  N44: 2_Channel_Relay1.K2-NO, Power_plug4.VCC
  N45: KY-1.NC, Power_plug5.VCC
  N46: KY-1.C, Power_plug3.VCC
  VSS: LCD1.Vss, LCM1602_IIC1.VSS
  VDD: LCD1.Vdd, LCM1602_IIC1.VDD
  N47: LCD1.Vo, LCM1602_IIC1.V0
  N48: LCD1.RS, LCM1602_IIC1.RS
  N49: LCD1.R/W, LCM1602_IIC1.RW
  N50: LCD1.E, LCM1602_IIC1.E
  N51: LCD1.DB0, LCM1602_IIC1.D0
  N52: LCD1.DB1, LCM1602_IIC1.D1
  N53: LCD1.DB2, LCM1602_IIC1.D2
  N54: LCD1.DB3, LCM1602_IIC1.D3
  N55: LCD1.DB4, LCM1602_IIC1.D4
  N56: LCD1.DB5, LCM1602_IIC1.D5
  N57: LCD1.DB6, LCM1602_IIC1.D6
  N58: LCD1.DB7, LCM1602_IIC1.D7
  N59: LCD1.A_+, LCM1602_IIC1.A
  N60: LCD1.K_-, LCM1602_IIC1.K

notes:
  INPUT PLN
  INPUT Inverter
  Mesin Air
  Output AC Rumah
  Led Indikator
  Auto/Manual
  Inverter & Tracker
  Input 5V
  elco 1uf 50v
  Radar Mesin Air
  Led tracker
  & LVD
  Motor Actuator
  Limit switch didalam
  actuator
  Fuse
  elco 1uf, 50v
  saklar auto/man
  direction & inverter
  i2c lcd module
  lcd 2004
  L298N

custom parts:
  Solar Charge Controller: PWM-Solar Charge Controller
  Solar Panel: Renogy 50 Watts 12 Volt Solar Panel
  NodeMCU V1.0: ESP8266 based NodeMCU
  H-Bridge with L298N: h-bridge
  D2F-FL Omron Snap Action Limit Switch with Level: Snap action switch with stainless steel lever.
  2 Channel Power Relay: A 2 channel power relay. The module operates at 5V.
  Keyes Relay: The Keyes 5V relay module is suitable for SCM development, home appliance control. It uses a 5V~12V TIL control signal which can control DC / AC signal.
  20x4 LCD display: 20x4 character display. CHECK LED POLARITY BEFORE CONNECTING POWER Some versions of the dispaly have the polarity of the LED pins "A" and "K" reversed.
  ACS712 Current Sensor: A breakout board for the Allegro ACS712 is a Hall Effect-based linear current sensor. The module operates at 5V.
  LCM1602 IIC: I2C-Module to use a 1602 or 2004 LCD on with the wire.h libory Serial LCD Modul
